// Logisim project circuito add-4.circ as structural Verilog: 3 circuits, main circuit main
module main (
  input  [3:0] in_1,
  input  [3:0] in_2,
  output Carry,
  output [3:0] out_4
);

  ADD_4 add_4_1 (.A(in_1), .B(in_2), .Soma(out_4), .Overflow(Carry), .in_3(1'b0));
endmodule

module ADD_1 (
  input  A,
  input  B,
  input  C,
  output S,
  output V
);

  wire and_1_out, and_2_out, and_3_out, and_4_out, and_5_out, and_6_out, and_7_out, and_8_out;

  and and_1 (and_1_out, ~A, ~B, C);  // AND_Gate
  and and_2 (and_2_out, ~A, B, ~C);  // AND_Gate
  and and_3 (and_3_out, A, ~B, ~C);  // AND_Gate
  and and_4 (and_4_out, A, B, C);
  and and_5 (and_5_out, ~A, B, C);  // AND_Gate
  and and_6 (and_6_out, A, ~B, C);  // AND_Gate
  and and_7 (and_7_out, A, B, ~C);  // AND_Gate
  and and_8 (and_8_out, A, B, C);
  or or_1 (S, and_1_out, and_2_out, and_3_out, and_4_out);
  or or_2 (V, and_5_out, and_6_out, and_7_out, and_8_out);
endmodule

module ADD_4 (
  input  [3:0] B,
  input  [3:0] A,
  input  in_3,
  output Overflow,
  output [3:0] Soma
);

  wire add_1_2_v, add_1_3_v, add_1_4_v;

  // Probe on B
  ADD_1 add_1_1 (.S(Soma[3]), .V(Overflow), .A(A[3]), .B(B[3]), .C(add_1_2_v));
  ADD_1 add_1_2 (.S(Soma[2]), .V(add_1_2_v), .A(A[2]), .B(B[2]), .C(add_1_3_v));
  // Probe on Soma
  ADD_1 add_1_3 (.S(Soma[1]), .V(add_1_3_v), .A(A[1]), .B(B[1]), .C(add_1_4_v));
  // Probe on A
  ADD_1 add_1_4 (.S(Soma[0]), .V(add_1_4_v), .A(A[0]), .B(B[0]), .C(in_3));
endmodule
